# Fritzing sketch Printplade (saved by Fritzing 0.9.3b)
circuit board: 8.46667cm x 5.64444cm
breadboards: 1

parts:
  Part1 = Arduino Mega 2560 (Rev3)
  MIC1 = Microphone
  J1 = Screw terminal - 2 pins [package=THT]

nets:
  N1: Part1.A0, Part1.GND, Part1.D46, MIC1.pin1, MIC1.pin2, J1.pin1, J1.pin2
